# Fritzing sketch ProiectDimi_cef (1) (saved by Fritzing 1.0.6)
perfboards: 2

parts:
  C7 = Ceramic Capacitor [capacitance=10nF voltage=35V package="100 mil [THT, multilayer]"]
  C2 = Ceramic Capacitor [capacitance=22nF voltage=35V package="100 mil [THT, multilayer]"]
  C7_2 = Ceramic Capacitor [capacitance=10nF voltage=35V package="100 mil [THT, multilayer]"]
  P6 = Rotary Potentiometer (Small) [maximum_resistance=10kΩ knob_status=50% power=0.5W package=THT]
  P3 = Rotary Potentiometer (Small) [maximum_resistance=10kΩ knob_status=50% power=0.5W package=THT]
  VCC1 = Battery [internal_resistance=0.1Ω]  # not connected
  Q2 = NPN-Transistor [package="TO92 [THT]"]
  Q1 = NPN-Transistor [package="TO92 [THT]"]
  Q3 = NPN-Transistor [package="TO92 [THT]"]
  Q4 = NPN-Transistor [package="TO92 [THT]"]
  R26 = Resistor [tolerance=±5% power=0.25W resistance=100 package=THT]
  R4 = Resistor [tolerance=±5% power=0.25W resistance=100 package=THT]
  R5 = Resistor [tolerance=±5% power=0.25W resistance=330 package=THT]
  R6 = Resistor [tolerance=±5% power=0.25W resistance=2.2k package=THT]
  R7 = Resistor [tolerance=±5% power=0.25W resistance=2.2k package=THT]
  C4 = Ceramic Capacitor [capacitance=10nF voltage=35V package="100 mil [THT, multilayer]"]
  C5 = Ceramic Capacitor [capacitance=10nF voltage=35V package="100 mil [THT, multilayer]"]
  C8 = Ceramic Capacitor [capacitance=22nF voltage=35V package="100 mil [THT, multilayer]"]
  P5 = Rotary Potentiometer (Small) [maximum_resistance=10kΩ knob_status=50% power=0.5W package=THT]
  P2 = Rotary Potentiometer (Small) [maximum_resistance=10kΩ knob_status=50% power=0.5W package=THT]
  P4 = Rotary Potentiometer (Small) [maximum_resistance=50kΩ knob_status=50% power=0.5W package=THT]
  RL = Resistor [tolerance=±5% power=0.5W resistance=680 package=THT]
  R12 = Resistor [tolerance=±5% power=0.25W resistance=2k package=THT]
  D1 = Rectifier Diode [part_number=1N4001 package="300 mil [THT]"]
  C3 = Ceramic Capacitor [capacitance=100nF voltage=35V package="100 mil [THT, multilayer]"]
  R13 = Resistor [tolerance=±5% power=0.25W resistance=390k package=THT]
  R14 = Resistor [tolerance=±5% power=0.25W resistance=100k package=THT]
  Q5 = Basic FET P-Channel [package="TO220 [THT]"]
  R15 = Resistor [tolerance=±5% power=0.25W resistance=10k package=THT]
  R16 = Resistor [tolerance=±5% power=0.25W resistance=22k package=THT]
  Q12 = PNP-Transistor [package="TO92 [THT]"]
  Q11 = PNP-Transistor [package="TO92 [THT]"]
  C8_2 = Ceramic Capacitor [capacitance=100nF voltage=35V package="100 mil [THT, multilayer]"]
  Q5_2 = NPN-Transistor [package="TO92 [THT]"]
  Q7 = PNP-Transistor [package="TO92 [THT]"]
  R17 = Resistor [tolerance=±5% power=0.25W resistance=220 package=THT]
  R18 = Resistor [tolerance=±5% power=0.25W resistance=100 package=THT]
  Q10 = NPN-Transistor [package="TO92 [THT]"]
  Q9 = PNP-Transistor [package="TO92 [THT]"]
  R30 = Resistor [tolerance=±5% power=0.25W resistance=0.47 package=THT]
  R31 = Resistor [tolerance=±5% power=0.25W resistance=0.47 package=THT]
  LED1 = LED - 5mm [color="Red (633nm)" current=0.030A package="5 mm [THT]"]

nets:
  N1: C7.1, C2.1, C7_2.1, P6.leg2, Q2.B, C4.0, C4.1, C5.0, C5.1, C8.0, C8.1, P5.leg1, P5.wiper
  N2: C2.0, C7_2.0
  N3: P6.leg1, P6.wiper, P3.leg1
  N4: P3.wiper, P3.leg2
  N5: Q2.E, Q1.C, Q3.C, Q12.B, Q12.C
  N6: Q2.C, Q11.C, C8_2.0, Q5_2.B
  N7: Q1.B, R15.Pin_1, R16.Pin_1
  N8: Q3.E, R26.Pin_1
  N9: Q3.B, Q4.B, Q4.C, R5.Pin_0, Q7.B
  N10: Q4.E, R4.Pin_1
  N11: R26.Pin_0, R4.Pin_0, R18.Pin_1
  N12: R5.Pin_1, R6.Pin_0
  N13: R6.Pin_1, R7.Pin_1
  N14: R7.Pin_0, Q10.C, LED1.anode
  N15: P5.leg2, P2.leg1, P2.wiper
  N16: P2.leg2, R12.Pin_0, R16.Pin_0
  N17: P4.wiper, RL.Pin_0
  N18: P4.leg2, RL.Pin_1
  N19: R12.Pin_1, D1.cathode
  N20: D1.anode, C3.0, R13.Pin_0
  N21: C3.1, R14.Pin_0, Q5.source
  N22: R13.Pin_1, R14.Pin_1, Q5.gate
  N23: Q5.drain, R15.Pin_0
  N24: Q12.E, Q11.E, Q5_2.E
  N25: C8_2.1, Q7.C, Q10.B, Q9.B
  N26: Q7.E, R18.Pin_0
  N27: R17.Pin_1, LED1.cathode
  N28: Q10.E, R31.Pin_0
  N29: Q9.E, R30.Pin_0
  N30: R30.Pin_1, R31.Pin_1

notes:
  OUTPUT
  GROUND
